# Fritzing sketch rocker (saved by Fritzing 0.9.3b)
breadboards: 1

parts:
  Εξάρτημα1 = InvenSense MPU6050
  OLED_I2C1 = OLED 128x64 I2C Monochrome Display
  MCU1 = Raspberry Pi Zero

nets:
  VCC: Εξάρτημα1.VCC, OLED_I2C1.VDD, MCU1.pin_1, MCU1.pin_17
  GND: Εξάρτημα1.GND, OLED_I2C1.GND, MCU1.pin_6, MCU1.pin_9, MCU1.pin_39
  N1: Εξάρτημα1.SCL, OLED_I2C1.SCK, MCU1.pin_5
  N2: Εξάρτημα1.SDA, OLED_I2C1.SDA, MCU1.pin_3

notes:
  IOTA Powered Baby Rocker
